// Logisim project ALU.circ as structural Verilog
module _1_bit_Adder (
  input  Cin,
  input  A,
  input  B,
  output Sum,
  output Cout
);

  wire and_1_out, and_2_out, xor_1_out;

  xor xor_1 (xor_1_out, Cin, A);
  xor xor_2 (Sum, xor_1_out, B);
  and and_1 (and_1_out, A, Cin);
  and and_2 (and_2_out, xor_1_out, B);
  or or_1 (Cout, and_1_out, and_2_out);
endmodule
