// Logisim project BasicProcessor.circ as structural Verilog: 8 circuits, main circuit Basic Processor
module Basic_Processor (
  input  [5:0] Instr,
  input  [4:0] Rs,
  input  [4:0] Rt,
  input  [4:0] Rd,
  input  [15:0] Imm,
  input  [4:0] Shamt,
  output [15:0] out_7
);

  wire clock_1_out, control_1_multop, control_1_regwrite;
  wire [15:0] register_file_1_read_a, register_file_1_read_b;

  Control control_1 (.in_1(Instr), .RegWrite(control_1_regwrite), .multOP(control_1_multop));
  Register_File register_file_1 (
    .Write_Data(out_7), .A_Address(Rs), .B_Address(Rt), .RegWrite(control_1_regwrite), .Write_Address(Rd),
    .Read_A(register_file_1_read_a), .Read_B(register_file_1_read_b), .Clock(clock_1_out));
  Clock clock_1 (.out(clock_1_out));
  ALU alu_1 (
    .multOp(control_1_multop), .A(register_file_1_read_a), .B(register_file_1_read_b), .Clock(clock_1_out),
    .imm(Imm), .shamt(Shamt), .Opcode(Instr), .out_8(out_7));
endmodule

module ALU (
  input  multOp,
  input  [15:0] A,
  input  [15:0] B,
  input  Clock,
  input  [15:0] imm,
  input  [4:0] shamt,
  input  [5:0] Opcode,
  output [15:0] out_8
);

  wire comparator_1_lt;
  wire [15:0] and_1_out, hi_q, low_q, multiplexer_1_out, n16_bit_adder_1_sum, n16_bit_adder_2_sum, or_1_out,
       shifter_1_out, signed_multiplier_1_hi, signed_multiplier_1_lo, subtractor_1_out;

  Signed_Multiplier signed_multiplier_1 (.A(A), .B(B), .Hi(signed_multiplier_1_hi), .Lo(signed_multiplier_1_lo));
  Register #(.width(16)) low (.D(signed_multiplier_1_lo), .en(multOp), .Q(low_q), .clk(Clock));  // open: clr
  Register #(.width(16)) hi (.D(signed_multiplier_1_hi), .en(multOp), .Q(hi_q), .clk(Clock));  // open: clr
  _16_Bit_Adder u_16_bit_adder_1 (.A(A), .B(B), .Sum(n16_bit_adder_1_sum));  // open: Cout
  Subtractor #(.width(16)) subtractor_1 (.a(A), .b(B), .out(subtractor_1_out));  // open: bin, bout
  assign and_1_out = A & B;  // AND_Gate and_1, 16 bits wide
  assign or_1_out = A | B;  // OR_Gate or_1, 16 bits wide
  _16_Bit_Adder u_16_bit_adder_2 (.A(A), .B(imm), .Sum(n16_bit_adder_2_sum));  // open: Cout
  Shifter #(.width(16)) shifter_1 (.in(A), .\dist (shamt[3:0]), .out(shifter_1_out));
  Comparator #(.width(16)) comparator_1 (.a(A), .b(B), .lt(comparator_1_lt));  // open: gt, eq
  Multiplexer #(.width(16), .enable("false")) multiplexer_1 (
    .in0({16{1'b0}}), .in1(16'h1), .out(multiplexer_1_out), .sel(comparator_1_lt));
  Multiplexer #(.select(4), .width(16), .enable("false")) multiplexer_2 (
    .in0(n16_bit_adder_1_sum), .in1(subtractor_1_out), .in2({16{1'b0}}), .in3(and_1_out), .in4(or_1_out),
    .in5(n16_bit_adder_2_sum), .in6(shifter_1_out), .in7(multiplexer_1_out), .in8(hi_q), .in9(low_q),
    .in10({16{1'b0}}), .in11({16{1'b0}}), .in12({16{1'b0}}), .in13({16{1'b0}}), .in14({16{1'b0}}),
    .in15({16{1'b0}}), .out(out_8), .sel(Opcode[3:0]));
endmodule

module Register_File (
  input  [15:0] Write_Data,
  input  [4:0] A_Address,
  input  [4:0] B_Address,
  input  RegWrite,
  input  [4:0] Write_Address,
  input  Clock,
  output [15:0] Read_A,
  output [15:0] Read_B
);

  wire decoder_1_out0, decoder_1_out1, decoder_1_out2, decoder_1_out3, decoder_1_out4, decoder_1_out5,
       decoder_1_out6, decoder_1_out7, decoder_1_out8, decoder_1_out9, decoder_1_out10, decoder_1_out11,
       decoder_1_out12, decoder_1_out13, decoder_1_out14, decoder_1_out15;
  wire [15:0] register_1_q, register_2_q, register_3_q, register_4_q, register_5_q, register_6_q,
       register_7_q, register_8_q, register_9_q, register_10_q, register_11_q, register_12_q, register_13_q,
       register_14_q, register_15_q, register_16_q;

  Decoder #(.select(4)) decoder_1 (
    .out0(decoder_1_out0), .out1(decoder_1_out1), .out2(decoder_1_out2), .out3(decoder_1_out3),
    .out4(decoder_1_out4), .out5(decoder_1_out5), .out6(decoder_1_out6), .out7(decoder_1_out7),
    .out8(decoder_1_out8), .out9(decoder_1_out9), .out10(decoder_1_out10), .out11(decoder_1_out11),
    .out12(decoder_1_out12), .out13(decoder_1_out13), .out14(decoder_1_out14), .out15(decoder_1_out15),
    .sel(Write_Address[3:0]), .en(RegWrite));
  Register #(.width(16)) register_1 (.D(Write_Data), .en(decoder_1_out0), .Q(register_1_q), .clk(Clock));  // open: clr
  Register #(.width(16)) register_2 (.D(Write_Data), .en(decoder_1_out1), .Q(register_2_q), .clk(Clock));  // open: clr
  Register #(.width(16)) register_3 (.D(Write_Data), .en(decoder_1_out2), .Q(register_3_q), .clk(Clock));  // open: clr
  Register #(.width(16)) register_4 (.D(Write_Data), .en(decoder_1_out3), .Q(register_4_q), .clk(Clock));  // open: clr
  Register #(.width(16)) register_5 (.D(Write_Data), .en(decoder_1_out4), .Q(register_5_q), .clk(Clock));  // open: clr
  Register #(.width(16)) register_6 (.D(Write_Data), .en(decoder_1_out5), .Q(register_6_q), .clk(Clock));  // open: clr
  Register #(.width(16)) register_7 (.D(Write_Data), .en(decoder_1_out6), .Q(register_7_q), .clk(Clock));  // open: clr
  Register #(.width(16)) register_8 (.D(Write_Data), .en(decoder_1_out7), .Q(register_8_q), .clk(Clock));  // open: clr
  Register #(.width(16)) register_9 (.D(Write_Data), .en(decoder_1_out8), .Q(register_9_q), .clk(Clock));  // open: clr
  Register #(.width(16)) register_10 (
    .D(Write_Data), .en(decoder_1_out9), .Q(register_10_q), .clk(Clock));  // open: clr
  Register #(.width(16)) register_11 (
    .D(Write_Data), .en(decoder_1_out10), .Q(register_11_q), .clk(Clock));  // open: clr
  Register #(.width(16)) register_12 (
    .D(Write_Data), .en(decoder_1_out11), .Q(register_12_q), .clk(Clock));  // open: clr
  Register #(.width(16)) register_13 (
    .D(Write_Data), .en(decoder_1_out12), .Q(register_13_q), .clk(Clock));  // open: clr
  Register #(.width(16)) register_14 (
    .D(Write_Data), .en(decoder_1_out13), .Q(register_14_q), .clk(Clock));  // open: clr
  Register #(.width(16)) register_15 (
    .D(Write_Data), .en(decoder_1_out14), .Q(register_15_q), .clk(Clock));  // open: clr
  Register #(.width(16)) register_16 (
    .D(Write_Data), .en(decoder_1_out15), .Q(register_16_q), .clk(Clock));  // open: clr
  Multiplexer #(.select(4), .width(16), .enable("false")) multiplexer_1 (
    .in0(register_1_q), .in1(register_2_q), .in2(register_3_q), .in3(register_4_q), .in4(register_5_q),
    .in5(register_6_q), .in6(register_7_q), .in7(register_8_q), .in8(register_9_q), .in9(register_10_q),
    .in10(register_11_q), .in11(register_12_q), .in12(register_13_q), .in13(register_14_q),
    .in14(register_15_q), .in15(register_16_q), .out(Read_A), .sel(A_Address[3:0]));
  Multiplexer #(.select(4), .width(16), .enable("false")) multiplexer_2 (
    .in0(register_1_q), .in1(register_2_q), .in2(register_3_q), .in3(register_4_q), .in4(register_5_q),
    .in5(register_6_q), .in6(register_7_q), .in7(register_8_q), .in8(register_9_q), .in9(register_10_q),
    .in10(register_11_q), .in11(register_12_q), .in12(register_13_q), .in13(register_14_q),
    .in14(register_15_q), .in15(register_16_q), .out(Read_B), .sel(B_Address[3:0]));
endmodule

module Control (
  input  [5:0] in_1,
  output RegWrite,
  output multOP
);

  wire comparator_1_lt, or_1_out;

  Comparator #(.width(3), .mode("unsigned")) comparator_1 (
    .a(in_1[2:0]), .b(3'b011), .lt(comparator_1_lt));  // open: gt, eq
  Comparator #(.width(6)) comparator_2 (.a(in_1), .b(6'b000010), .eq(multOP));  // open: gt, lt
  or or_1 (or_1_out, ~in_1[3], comparator_1_lt);  // OR_Gate
  and and_1 (RegWrite, or_1_out, ~multOP);  // AND_Gate
endmodule

// Mul
module Signed_Multiplier (
  input  [15:0] A,
  input  [15:0] B,
  output [15:0] Hi,
  output [15:0] Lo
);

  wire [31:0] bit_extender_1_out, bit_extender_2_out;

  assign bit_extender_1_out = {{16{A[15]}}, A};  // Bit_Extender bit_extender_1
  Multiplier #(.width(32)) multiplier_1 (
    .a(bit_extender_1_out), .b(bit_extender_2_out), .out({Hi, Lo}));  // open: cin, cout
  assign bit_extender_2_out = {{16{B[15]}}, B};  // Bit_Extender bit_extender_2
endmodule

// Adder
module _16_Bit_Adder (
  input  [15:0] A,
  input  [15:0] B,
  output [15:0] Sum,
  output Cout
);

  wire n4_bit_adder_1_cout, n4_bit_adder_2_cout, n4_bit_adder_3_cout;

  _4_bit_Adder u_4_bit_adder_1 (.Cin(1'b0), .A(A[3:0]), .B(B[3:0]), .Sum(Sum[3:0]), .Cout(n4_bit_adder_1_cout));
  _4_bit_Adder u_4_bit_adder_2 (
    .Cin(n4_bit_adder_1_cout), .A(A[7:4]), .B(B[7:4]), .Sum(Sum[7:4]), .Cout(n4_bit_adder_2_cout));
  _4_bit_Adder u_4_bit_adder_3 (
    .Cin(n4_bit_adder_2_cout), .A(A[11:8]), .B(B[11:8]), .Sum(Sum[11:8]), .Cout(n4_bit_adder_3_cout));
  _4_bit_Adder u_4_bit_adder_4 (.Cin(n4_bit_adder_3_cout), .A(A[15:12]), .B(B[15:12]), .Sum(Sum[15:12]), .Cout(Cout));
endmodule

module _4_bit_Adder (
  input  Cin,
  input  [3:0] A,
  input  [3:0] B,
  output [3:0] Sum,
  output Cout
);

  wire n1_bit_adder_1_cout, n1_bit_adder_2_cout, n1_bit_adder_3_cout;

  _1_bit_Adder u_1_bit_adder_1 (.Cin(Cin), .A(A[0]), .B(B[0]), .Sum(Sum[0]), .Cout(n1_bit_adder_1_cout));
  _1_bit_Adder u_1_bit_adder_2 (
    .Cin(n1_bit_adder_1_cout), .A(A[1]), .B(B[1]), .Sum(Sum[1]), .Cout(n1_bit_adder_2_cout));
  _1_bit_Adder u_1_bit_adder_3 (
    .Cin(n1_bit_adder_2_cout), .A(A[2]), .B(B[2]), .Sum(Sum[2]), .Cout(n1_bit_adder_3_cout));
  _1_bit_Adder u_1_bit_adder_4 (.Cin(n1_bit_adder_3_cout), .A(A[3]), .B(B[3]), .Sum(Sum[3]), .Cout(Cout));
endmodule

module _1_bit_Adder (
  input  Cin,
  input  A,
  input  B,
  output Sum,
  output Cout
);

  wire and_1_out, and_2_out, xor_1_out;

  xor xor_1 (xor_1_out, Cin, A);
  xor xor_2 (Sum, xor_1_out, B);
  and and_1 (and_1_out, A, Cin);
  and and_2 (and_2_out, xor_1_out, B);
  or or_1 (Cout, and_1_out, and_2_out);
endmodule
